# Fritzing sketch iEEGSynchroniser (saved by Fritzing 0.9.3b)
breadboards: 1

parts:
  Part1 = Arduino Leonardo (Rev3b)
  S1 = Pushbutton [package="[THT]"]
  S2 = Pushbutton [package="[THT]"]
  S3 = Pushbutton [package="[THT]"]
  S4 = Pushbutton [package="[THT]"]
  R2 = Resistor [tolerance=±5% resistance=220 package=THT]
  R3 = Photocell (LDR) [package=THT]
  Part2 = DB25M

nets:
  N1: Part1.D4/A6, S4.Pin_3, S4.Pin_4
  N2: Part1.D5_PWM, S3.Pin_3, S3.Pin_4
  N3: Part1.D6_PWM/A7, S2.Pin_3, S2.Pin_4
  N4: Part1.D7, S1.Pin_3, S1.Pin_4
  N5: Part1.5V, R2.Pin_0
  N6: Part1.GND, S1.Pin_1, S1.Pin_2, S2.Pin_1, S2.Pin_2, S3.Pin_1, S3.Pin_2, S4.Pin_1, S4.Pin_2, R3.pin_1, Part2.pin18
  N7: Part1.D13_PWM, Part2.pin1
  N8: R2.Pin_1, R3.pin_0
